// Logisim project CPU.circ as structural Verilog: 10 circuits, main circuit main
module main (
  input  [3:0] RsX,
  input  [7:0] Ix,
  input  [3:0] RsY,
  input  [7:0] Iy,
  input  [3:0] Rd,
  input  rwctl,
  input  [11:0] \Instrução ,
  output R0,
  output [7:0] Out_ULA,
  output [7:0] Rx,
  output [7:0] Ry,
  output [3:0] out_12,
  output [3:0] out_13,
  output [3:0] out_14
);

  wire rmctl_rwctl, rwctl_t;
  wire [1:0] pcctl, rdctl;
  wire [2:0] rinctl;
  wire [3:0] Rd_t;
  wire [7:0] IR, \Memória , OUT_rinctl, PC;

  IDEC idec_1 (.\INSTRUÇÃO (\Instrução ), .Menor(out_14), .Meio(out_13), .Op(out_12));
  CTLU ctlu_1 (
    .Op(out_12), .R0(R0), .rwctl(rwctl_t), .rinctl(rinctl), .rdctl(rdctl), .rmctl_wmctl(rmctl_rwctl),
    .pcctl(pcctl));
  Multiplexer #(.select(3), .width(8), .enable("false")) multiplexer_1 (
    .in0(Out_ULA), .in1(\Memória ), .in2(IR), .in3(OUT_rinctl), .in4(PC), .out(OUT_rinctl), .sel(rinctl));  // open: in5, in6, in7
  Registrador registrador_1 (
    .RsX(RsX), .RsY(RsY), .Rd(Rd_t), .Rin(OUT_rinctl), .rwctl(rwctl_t), .R0(R0), .Rx(Rx), .Ry(Ry));
  \Unidade_Lógica_Aritimética  \unidade_lógica_aritimética_1  (.Ix(Ix), .Iy(Iy), .Op(out_12), .Out(Out_ULA));

  // Other names for the same wires on the sheet: Instrucao[11:0] = \Instrução ; Meio[3:0] = out_13;
  //   Menor[3:0] = out_14; Op[3:0] = out_12; Rin[7:0] = OUT_rinctl

  // Notes on the sheet:
  //   ENTRADAS E SAÍDAS SEPARADAS ULA
  //   ENTRADAS E SAÍDAS SEPARADAS IDEC
  //   ENTRADAS E SAÍDAS SEPARADAS REG
  //   ENTRADAS E SAÍDAS SEPARADAS IDEC
endmodule

// REG
module Registrador (
  input  [3:0] RsX,
  input  [3:0] RsY,
  input  [3:0] Rd,
  input  [7:0] Rin,
  input  rwctl,
  output R0,
  output [7:0] Rx,
  output [7:0] Ry
);

  wire comparator_1_eq, demultiplexer_1_out1, demultiplexer_1_out2, demultiplexer_1_out3,
       demultiplexer_1_out4, demultiplexer_1_out5, demultiplexer_1_out6, demultiplexer_1_out7,
       demultiplexer_1_out8, demultiplexer_1_out9, demultiplexer_1_out10, demultiplexer_1_out11,
       demultiplexer_1_out12, demultiplexer_1_out13, demultiplexer_1_out14, demultiplexer_1_out15, not_1_out,
       undriven;
  wire [7:0] register_1_q, register_2_q, register_3_q, register_4_q, register_5_q, register_6_q,
       register_7_q, register_8_q, register_9_q, register_10_q, register_11_q, register_12_q, register_13_q,
       register_14_q, register_15_q;

  not not_1 (not_1_out, rwctl);
  Demultiplexer #(.select(4), .enable("false")) demultiplexer_1 (
    .out1(demultiplexer_1_out1), .out2(demultiplexer_1_out2), .out3(demultiplexer_1_out3),
    .out4(demultiplexer_1_out4), .out5(demultiplexer_1_out5), .out6(demultiplexer_1_out6),
    .out7(demultiplexer_1_out7), .out8(demultiplexer_1_out8), .out9(demultiplexer_1_out9),
    .out10(demultiplexer_1_out10), .out11(demultiplexer_1_out11), .out12(demultiplexer_1_out12),
    .out13(demultiplexer_1_out13), .out14(demultiplexer_1_out14), .out15(demultiplexer_1_out15),
    .in(not_1_out), .sel(Rd));  // open: out0
  not not_2 (R0, comparator_1_eq);
  Comparator comparator_1 (.a({8{1'b0}}), .b(Rin), .eq(comparator_1_eq));  // open: gt, lt
  Register register_1 (.D(Rin), .Q(register_1_q), .clk(demultiplexer_1_out1));  // open: en, clr
  Register register_2 (.D(Rin), .Q(register_2_q), .clk(demultiplexer_1_out2));  // open: en, clr
  Register register_3 (.D(Rin), .Q(register_3_q), .clk(demultiplexer_1_out3));  // open: en, clr
  Register register_4 (.D(Rin), .Q(register_4_q), .clk(demultiplexer_1_out4));  // open: en, clr
  Register register_5 (.D(Rin), .Q(register_5_q), .clk(demultiplexer_1_out5));  // open: en, clr
  Register register_6 (.D(Rin), .Q(register_6_q), .clk(demultiplexer_1_out6));  // open: en, clr
  Register register_7 (.D(Rin), .Q(register_7_q), .clk(demultiplexer_1_out7));  // open: en, clr
  Register register_8 (.D(Rin), .en(undriven), .Q(register_8_q), .clk(demultiplexer_1_out8));  // open: clr
  Register register_9 (.D(Rin), .Q(register_9_q), .clk(demultiplexer_1_out9));  // open: en, clr
  Register register_10 (.D(Rin), .Q(register_10_q), .clk(demultiplexer_1_out10));  // open: en, clr
  Register register_11 (.D(Rin), .Q(register_11_q), .clk(demultiplexer_1_out11));  // open: en, clr
  Register register_12 (.D(Rin), .Q(register_12_q), .clk(demultiplexer_1_out12));  // open: en, clr
  Register register_13 (.D(Rin), .Q(register_13_q), .clk(demultiplexer_1_out13));  // open: en, clr
  Register register_14 (.D(Rin), .Q(register_14_q), .clk(demultiplexer_1_out14));  // open: en, clr
  Register register_15 (.D(Rin), .Q(register_15_q), .clk(demultiplexer_1_out15));  // open: en, clr
  Multiplexer #(.select(4), .width(8), .enable("false")) multiplexer_1 (
    .in0(Rin), .in1(register_1_q), .in2(register_2_q), .in3(register_3_q), .in4(register_4_q),
    .in5(register_5_q), .in6(register_6_q), .in7(register_7_q), .in8(register_8_q), .in9(register_9_q),
    .in10(register_10_q), .in11(register_11_q), .in12(register_12_q), .in13(register_13_q),
    .in14(register_14_q), .in15(register_15_q), .out(Rx), .sel(RsX));
  Multiplexer #(.select(4), .width(8), .enable("false")) multiplexer_2 (
    .in0(Rin), .in1(register_1_q), .in2(register_2_q), .in3(register_3_q), .in4(register_4_q),
    .in5(register_5_q), .in6(register_6_q), .in7(register_7_q), .in8(register_8_q), .in9(register_9_q),
    .in10(register_10_q), .in11(register_11_q), .in12(register_12_q), .in13(register_13_q),
    .in14(register_14_q), .in15(register_15_q), .out(Ry), .sel(RsY));

  // Other names for the same wires on the sheet: Rs1[3:0] = RsX; Rs2[3:0] = RsY
endmodule

// ULA
module \Unidade_Lógica_Aritimética  (
  input  [7:0] Ix,
  input  [7:0] Iy,
  input  [3:0] Op,
  output [7:0] Out
);

  wire comparator_1_eq, comparator_2_eq, comparator_3_lt, comparator_4_eq, comparator_4_lt, or_2_out;
  wire [7:0] adder_1_out, and_1_out, bit_extender_1_out, bit_extender_2_out, bit_extender_3_out,
       bit_extender_4_out, divider_1_out, multiplier_1_out, or_1_out, subtractor_1_out;

  assign and_1_out = Ix & Iy;  // AND_Gate and_1, 8 bits wide
  assign or_1_out = Ix | Iy;  // OR_Gate or_1, 8 bits wide
  Comparator comparator_1 (.a({8{1'b0}}), .b(Iy), .eq(comparator_1_eq));  // open: gt, lt
  Adder adder_1 (.a(Ix), .b(Iy), .out(adder_1_out));  // open: cin, cout
  Subtractor subtractor_1 (.a(Ix), .b(Iy), .out(subtractor_1_out));  // open: bin, bout
  Multiplier multiplier_1 (.a(Ix), .b(Iy), .out(multiplier_1_out));  // open: cin, cout
  Divider divider_1 (.a(Ix), .b(Iy), .out(divider_1_out));  // open: upper, rem
  Comparator comparator_2 (.a(Ix), .b(Iy), .eq(comparator_2_eq));  // open: gt, lt
  Comparator comparator_3 (.a(Ix), .b(Iy), .lt(comparator_3_lt));  // open: gt, eq
  Comparator comparator_4 (.a(Ix), .b(Iy), .eq(comparator_4_eq), .lt(comparator_4_lt));  // open: gt
  assign bit_extender_1_out = {{7{1'b0}}, comparator_1_eq};  // Bit_Extender bit_extender_1
  or or_2 (or_2_out, comparator_4_eq, comparator_4_lt);
  assign bit_extender_2_out = {{7{1'b0}}, comparator_2_eq};  // Bit_Extender bit_extender_2
  assign bit_extender_3_out = {{7{1'b0}}, comparator_3_lt};  // Bit_Extender bit_extender_3
  assign bit_extender_4_out = {{7{1'b0}}, or_2_out};  // Bit_Extender bit_extender_4
  Multiplexer #(.select(4), .width(8), .enable("false")) multiplexer_1 (
    .in0(and_1_out), .in1(or_1_out), .in2(bit_extender_1_out), .in3(adder_1_out), .in4(subtractor_1_out),
    .in5(multiplier_1_out), .in6(divider_1_out), .in7(bit_extender_2_out), .in8(bit_extender_3_out),
    .in9(bit_extender_4_out), .out(Out), .sel(Op));  // open: in10, in11, in12, in13, in14, in15
endmodule

module REG_ULA (
  input  [3:0] RsX,
  input  [7:0] Ix,
  input  [3:0] RsY,
  input  [7:0] Iy,
  input  [3:0] Rd,
  input  [3:0] Op_ULA,
  input  rwctl,
  input  [2:0] rinctl,
  output R0,
  output [7:0] Out_ULA,
  output [7:0] Rx,
  output [7:0] Ry
);

  wire [7:0] IR, \Memória , OUT_rinctl, PC;

  Registrador registrador_1 (.RsX(RsX), .RsY(RsY), .Rd(Rd), .Rin(OUT_rinctl), .rwctl(rwctl), .R0(R0), .Rx(Rx), .Ry(Ry));
  \Unidade_Lógica_Aritimética  \unidade_lógica_aritimética_1  (.Ix(Ix), .Iy(Iy), .Op(Op_ULA), .Out(Out_ULA));
  Multiplexer #(.select(3), .width(8), .enable("false")) multiplexer_1 (
    .in0(Out_ULA), .in1(\Memória ), .in2(IR), .in3(OUT_rinctl), .in4(PC), .out(OUT_rinctl), .sel(rinctl));  // open: in5, in6, in7

  // Other names for the same wires on the sheet: Op[3:0] = Op_ULA; Rin[7:0] = OUT_rinctl

  // Notes on the sheet:
  //   ENTRADAS E SAÍDAS SEPARADAS ULA
  //   ENTRADAS E SAÍDAS SEPARADAS REG
endmodule

module IDEC (
  input  [11:0] \INSTRUÇÃO ,
  output [3:0] Menor,
  output [3:0] Meio,
  output [3:0] Op
);


  assign Meio = \INSTRUÇÃO [7:4];
  assign Menor = \INSTRUÇÃO [3:0];
  assign Op = \INSTRUÇÃO [11:8];
endmodule

module CTLU (
  input  [3:0] Op,
  input  R0,
  output rwctl,
  output [2:0] rinctl,
  output [1:0] rdctl,
  output rmctl_wmctl,
  output [1:0] pcctl
);

  wire and_2_out;

  Multiplexer #(.select(4), .enable("false")) multiplexer_1 (
    .in0(1'b0), .in1(1'b0), .in2(1'b0), .in3(1'b0), .in4(1'b0), .in5(1'b0), .in6(1'b0), .in7(1'b0),
    .in8(1'b0), .in9(1'b0), .in10(1'b0), .in11(1'b0), .in12(1'b1), .in13(1'b0), .in14(1'b0), .in15(1'b0),
    .out(rwctl), .sel(Op));
  Multiplexer #(.select(4), .width(3), .enable("false")) multiplexer_2 (
    .in0(3'b000), .in1(3'b000), .in2(3'b000), .in3(3'b000), .in4(3'b000), .in5(3'b000), .in6(3'b000),
    .in7(3'b000), .in8(3'b000), .in9(3'b000), .in10(3'b001), .in11(3'b010), .in12(3'b000), .in13(3'b011),
    .in14(3'b100), .in15(3'b000), .out(rinctl), .sel(Op));
  and and_1 (pcctl[1], Op[3], Op[2], Op[1], ~Op[0], R0);  // AND_Gate
  and and_2 (and_2_out, ~Op[0], ~R0);  // AND_Gate
  Multiplexer #(.select(4), .width(2), .enable("false")) multiplexer_3 (
    .in0(2'b00), .in1(2'b00), .in2(2'b00), .in3(2'b00), .in4(2'b00), .in5(2'b00), .in6(2'b00), .in7(2'b00),
    .in8(2'b00), .in9(2'b00), .in10(2'b00), .in11(2'b00), .in12(2'b10), .in13(2'b10), .in14(2'b01),
    .in15(2'b01), .out(rdctl), .sel(Op));
  or or_1 (pcctl[0], and_2_out, ~Op[3], ~Op[2], ~Op[1]);  // OR_Gate
  Multiplexer #(.select(4), .enable("false")) multiplexer_4 (
    .in0(1'b0), .in1(1'b0), .in2(1'b0), .in3(1'b0), .in4(1'b0), .in5(1'b0), .in6(1'b0), .in7(1'b0),
    .in8(1'b0), .in9(1'b0), .in10(1'b1), .in11(1'b0), .in12(1'b1), .in13(1'b0), .in14(1'b0), .in15(1'b0),
    .out(rmctl_wmctl), .sel(Op));
endmodule

module IDEC___testes (
  output [7:0] OutULA,
  output ALU_MOV,
  output NOT,
  output LDA_STR_JMP,
  output LDI,
  output HLT
);

  wire [2:0] teste;
  wire [3:0] Cod_Op, Mais_Sig, Menos_Sig, Op;
  wire [7:0] bit_extender_1_out, bit_extender_2_out, bit_extender_3_out, bit_extender_4_out,
       bit_extender_5_out, bit_extender_6_out, bit_extender_7_out;

  assign bit_extender_1_out = {{4{1'b0}}, Mais_Sig};  // Bit_Extender bit_extender_1
  assign bit_extender_2_out = {{4{1'b0}}, Menos_Sig};  // Bit_Extender bit_extender_2
  \Unidade_Lógica_Aritimética  \unidade_lógica_aritimética_1  (
    .Ix(bit_extender_1_out), .Iy(bit_extender_2_out), .Op(Op), .Out(OutULA));
  Multiplexer #(.select(4), .width(3), .enable("false")) multiplexer_1 (
    .in0(3'b000), .in1(3'b000), .in2(3'b001), .in3(3'b000), .in4(3'b000), .in5(3'b000), .in6(3'b000),
    .in7(3'b000), .in8(3'b000), .in9(3'b000), .in10(3'b010), .in11(3'b011), .in12(3'b010), .in13(3'b000),
    .in14(3'b010), .in15(3'b100), .out(teste), .sel(Cod_Op));
  assign bit_extender_3_out = {{5{1'b0}}, teste};  // Bit_Extender bit_extender_3
  assign bit_extender_4_out = {{5{1'b0}}, teste};  // Bit_Extender bit_extender_4
  assign bit_extender_5_out = {{5{1'b0}}, teste};  // Bit_Extender bit_extender_5
  assign bit_extender_6_out = {{5{1'b0}}, teste};  // Bit_Extender bit_extender_6
  assign bit_extender_7_out = {{5{1'b0}}, teste};  // Bit_Extender bit_extender_7
  Comparator comparator_1 (.a({8{1'b0}}), .b(bit_extender_3_out), .eq(ALU_MOV));  // open: gt, lt
  Comparator comparator_2 (.a(8'h1), .b(bit_extender_4_out), .eq(NOT));  // open: gt, lt
  Comparator comparator_3 (.a(8'h2), .b(bit_extender_5_out), .eq(LDA_STR_JMP));  // open: gt, lt
  Comparator comparator_4 (.a(8'h3), .b(bit_extender_6_out), .eq(LDI));  // open: gt, lt
  Comparator comparator_5 (.a(8'h4), .b(bit_extender_7_out), .eq(HLT));  // open: gt, lt

  // Notes on the sheet:
  //   ULA+IDEC
endmodule

module Memorias (
  input  [7:0] Adress_IM,
  input  [7:0] Adress_DM,
  output [11:0] Data_IM,
  output [7:0] Data_DM
);

  ROM #(.dataWidth(12)) rom_1 (.addr(Adress_IM), .data(Data_IM));  // open: sel
  RAM ram_1 (.addr(Adress_DM), .data(Data_DM));  // open: sel, clk, ld, clr

  // Notes on the sheet:
  //   ROM - Instruction Memory
  //   RAM - Data Memory
endmodule

module PC (
  input  [11:0] \Instrução ,
  input  [7:0] Dados_Contador_PC,
  output [3:0] out_3,
  output [3:0] out_4,
  output [3:0] out_5,
  output [7:0] Valor_Atual_PC
);

  wire bit_extender_1_out, clock_1_out, comparator_1_eq, not_1_out, R0, rmctl_rwctl, rwctl;
  wire [1:0] multiplexer_1_out, pcctl, rdctl, undriven;
  wire [2:0] rinctl;

  Multiplexer #(.select(2), .width(2), .enable("false")) multiplexer_1 (
    .in0(2'b00), .in1(2'b01), .in2(undriven), .out(multiplexer_1_out), .sel(pcctl));  // open: in3
  Bit_Extender #(.in_width(2), .out_width(1)) bit_extender_1 (.in(multiplexer_1_out), .out(bit_extender_1_out));
  not not_1 (not_1_out, bit_extender_1_out);
  Clock clock_1 (.out(clock_1_out));
  Comparator #(.width(1)) comparator_1 (.a(bit_extender_1_out), .b(1'b0), .eq(comparator_1_eq));  // open: gt, lt
  Counter counter_1 (
    .load(not_1_out), .D(Dados_Contador_PC), .count(bit_extender_1_out), .Q(Valor_Atual_PC),
    .clr(comparator_1_eq));  // open: carry, clk
  IDEC idec_1 (.\INSTRUÇÃO (\Instrução ), .Menor(out_5), .Meio(out_4), .Op(out_3));
  CTLU ctlu_1 (
    .Op(out_3), .R0(R0), .rwctl(rwctl), .rinctl(rinctl), .rdctl(rdctl), .rmctl_wmctl(rmctl_rwctl),
    .pcctl(pcctl));

  // Other names for the same wires on the sheet: Instrucao[11:0] = \Instrução ; Meio[3:0] = out_4; Menor[3:0] = out_5;
  //   Op[3:0] = out_3

  // Notes on the sheet:
  //   ENTRADAS E SAÍDAS SEPARADAS IDEC
endmodule

module teste (
  input  [3:0] RsX,
  input  [7:0] Ix,
  input  [3:0] RsY,
  input  [7:0] Iy,
  input  [3:0] Rd,
  input  rwctl,
  input  [11:0] \Instrução ,
  output R0,
  output [7:0] Out_ULA,
  output [7:0] Rx,
  output [7:0] Ry,
  output [3:0] out_12,
  output [3:0] out_13,
  output [3:0] out_14
);

  wire rmctl_rwctl, rwctl_t;
  wire [1:0] pcctl, rdctl;
  wire [2:0] rinctl;
  wire [7:0] IR, \Memória , OUT_rinctl, PC;

  IDEC idec_1 (.\INSTRUÇÃO (\Instrução ), .Menor(out_14), .Meio(out_13), .Op(out_12));
  CTLU ctlu_1 (
    .Op(out_12), .R0(R0), .rwctl(rwctl_t), .rinctl(rinctl), .rdctl(rdctl), .rmctl_wmctl(rmctl_rwctl),
    .pcctl(pcctl));
  Multiplexer #(.select(3), .width(8), .enable("false")) multiplexer_1 (
    .in0(Out_ULA), .in1(\Memória ), .in2(IR), .in3(OUT_rinctl), .in4(PC), .out(OUT_rinctl), .sel(rinctl));  // open: in5, in6, in7
  Registrador registrador_1 (
    .RsX(out_13), .RsY(out_14), .Rd(Rd), .Rin(OUT_rinctl), .rwctl(rwctl_t), .R0(R0), .Rx(Rx), .Ry(Ry));
  \Unidade_Lógica_Aritimética  \unidade_lógica_aritimética_1  (.Ix(Ix), .Iy(Iy), .Op(out_12), .Out(Out_ULA));

  // Other names for the same wires on the sheet: Instrucao[11:0] = \Instrução ; Meio[3:0] = out_13;
  //   Menor[3:0] = out_14; Op[3:0] = out_12; Rin[7:0] = OUT_rinctl

  // Notes on the sheet:
  //   ENTRADAS E SAÍDAS SEPARADAS ULA
  //   ENTRADAS E SAÍDAS SEPARADAS IDEC
  //   ENTRADAS E SAÍDAS SEPARADAS REG
  //   ENTRADAS E SAÍDAS SEPARADAS IDEC
endmodule
